# Fritzing sketch Prototype1 (saved by Fritzing 0.9.3b)
breadboards: 1

parts:
  Part1 = Arduino Uno (Rev3)
  U1 = LCD-16X2 [package=lcd-16x2]
  R1 = Resistor [tolerance=±5% resistance=220 package=THT]
  DS1 = DS18B20 1-Wire Temperature Sensor [part_number=DS18B20]
  R2 = Resistor [tolerance=±5% resistance=4.7k package="1206 [SMD]"]

nets:
  N1: Part1.D10_PWM/SS, DS1.DQ, R2.Pin_0
  N2: Part1.D11_PWM/MOSI, U1.E
  N3: Part1.D12/MISO, U1.RS
  GND: Part1.GND, U1.VSS, U1.VO, U1.R_W, U1.K, DS1.GND
  N4: Part1.D2, U1.DB4
  N5: Part1.D3_PWM, U1.DB5
  N6: Part1.D4, U1.DB6
  N7: Part1.D5_PWM, U1.DB7
  VDD: Part1.5V, U1.VDD, R1.Pin_0, DS1.VDD, R2.Pin_1
  N8: U1.A, R1.Pin_1
